# Fritzing sketch TrafficLight (saved by Fritzing 0.5.2b)
breadboards: 1

parts:
  Netduino1 = Netduino Plus
  Red_LED = Red LED - 5mm [package="5 mm [THT]"]
  Green_LED = green LED - 5mm [package="5 mm [THT]"]
  Yellow_LED = yellow LED - 5mm [package="5 mm [THT]"]

nets:
  N1: Netduino1.GND, Red_LED.cathode, Green_LED.cathode, Yellow_LED.cathode
  N2: Netduino1.D13_SPCK, Green_LED.anode
  N3: Netduino1.D12_MISO, Yellow_LED.anode
  N4: Netduino1.D11_MOSI, Red_LED.anode
